// Logisim project score.circ as structural Verilog: 4 circuits, main circuit clock
module clock (
  input  [7:0] \input ,
  output [3:0] tens,
  output [3:0] units
);

  wire [3:0] tens_units_1_out_tens, tens_units_2_out_tens, tens_units_3_out_tens, tens_units_4_out_tens,
       tens_units_6_out_tens;
  wire [7:0] tens_units_1_out_units, tens_units_2_out_units, tens_units_3_out_units, tens_units_4_out_units,
       tens_units_6_out_units;
  wire [7:4] tens_units_5_out_units;

  tens_units tens_units_1 (
    .in_units(\input ), .in_tens(4'b0000), .out_units(tens_units_1_out_units),
    .out_tens(tens_units_1_out_tens));
  tens_units tens_units_2 (
    .in_units(tens_units_1_out_units), .in_tens(tens_units_1_out_tens), .out_units(tens_units_2_out_units),
    .out_tens(tens_units_2_out_tens));
  tens_units tens_units_3 (
    .in_units(tens_units_4_out_units), .in_tens(tens_units_4_out_tens), .out_units(tens_units_3_out_units),
    .out_tens(tens_units_3_out_tens));
  tens_units tens_units_4 (
    .in_units(tens_units_2_out_units), .in_tens(tens_units_2_out_tens), .out_units(tens_units_4_out_units),
    .out_tens(tens_units_4_out_tens));
  tens_units tens_units_5 (
    .in_units(tens_units_6_out_units), .in_tens(tens_units_6_out_tens),
    .out_units({tens_units_5_out_units, units}), .out_tens(tens));
  tens_units tens_units_6 (
    .in_units(tens_units_3_out_units), .in_tens(tens_units_3_out_tens), .out_units(tens_units_6_out_units),
    .out_tens(tens_units_6_out_tens));
endmodule

module res_of_check (
  input  [7:0] A,
  input  sel,
  input  [7:0] B,
  output [7:0] res
);

  wire [7:0] and_1_out, and_2_out;
  wire [7:7] not_1_out;

  not not_1 (not_1_out[7], sel);
  assign and_1_out = A & {8{sel}};  // AND_Gate and_1, 8 bits wide
  assign and_2_out = {8{not_1_out[7]}} & B;  // AND_Gate and_2, 8 bits wide
  assign res = and_1_out | and_2_out;  // OR_Gate or_1, 8 bits wide
endmodule

module tens_units (
  input  [7:0] in_units,
  input  [3:0] in_tens,
  output [7:0] out_units,
  output [3:0] out_tens
);

  wire comparator_1_lt;
  wire [0:0] not_1_out;
  wire [7:0] subtractor_1_out;

  Comparator #(.mode("unsigned")) comparator_1 (.a(in_units), .b(8'ha), .lt(comparator_1_lt));  // open: gt, eq
  Subtractor subtractor_1 (.a(in_units), .b(8'ha), .out(subtractor_1_out));  // open: bin, bout
  not not_1 (not_1_out[0], comparator_1_lt);
  res_of_check res_of_check_1 (.A(in_units), .sel(comparator_1_lt), .B(subtractor_1_out), .res(out_units));
  Adder #(.width(4)) adder_1 (.a({3'b000, not_1_out[0]}), .b(in_tens), .out(out_tens));  // open: cin, cout
endmodule

module test (
  input  [7:0] in_1
);

  wire [3:0] clock_1_p1, clock_1_p3;

  Hex_Digit_Display hex_digit_display_1 (.value(clock_1_p1));  // open: dp
  // clock clock_1: pin names not known; wires that end beside it: clock_1_p1, in_1, clock_1_p3
  // Probe on in_1
  Hex_Digit_Display hex_digit_display_2 (.value(clock_1_p3));  // open: dp
endmodule
