// Logisim project tennis.circ as structural Verilog: 19 circuits, main circuit main
module main (
);

  wire leds_1_out_3, leds_1_out_4, leds_1_out_5, leds_1_out_6, leds_1_out_7, leds_1_out_8, leds_1_out_9,
       leds_1_out_10, leds_1_out_11, leds_1_out_12, leds_1_out_13, leds_1_out_14, leds_1_out_15,
       leds_1_out_16, leds_1_out_17, leds_1_out_18, leds_1_out_19, leds_1_out_20, leds_1_out_21,
       leds_1_out_22, leds_1_out_23, leds_1_out_24, leds_1_out_25, leds_1_out_26, leds_1_out_27,
       leds_1_out_28, leds_1_out_29, leds_1_out_30, leds_1_out_31, leds_1_out_32, leds_1_out_33,
       leds_1_out_34, Reset_out, Start_out;
  wire [1:0] joystick_1_y;
  wire [3:0] dial_1_tens, dial_1_units, dial_2_tens, dial_2_units;
  wire [4:0] kinematic_controller_1_ballx, kinematic_controller_1_bally, kinematic_controller_1_id,
       kinematic_controller_1_leftyout, kinematic_controller_1_rightyout, video_section_1_id_2,
       video_section_1_left_bat_2, video_section_1_right_bat_2, video_section_1_x_ball_2,
       video_section_1_y_ball_2, video_section_2_id_2, video_section_2_left_bat_2,
       video_section_2_right_bat_2, video_section_2_x_ball_2, video_section_2_y_ball_2, video_section_3_id_2,
       video_section_3_left_bat_2, video_section_3_right_bat_2, video_section_3_x_ball_2,
       video_section_3_y_ball_2;
  wire [7:0] cdm8_score, player_score;
  wire [31:0] video_section_1__0, video_section_1__1, video_section_1__2, video_section_1__3,
       video_section_1__4, video_section_1__5, video_section_1__6, video_section_1__7, video_section_2__0,
       video_section_2__1, video_section_2__2, video_section_2__3, video_section_2__4, video_section_2__5,
       video_section_2__6, video_section_2__7, video_section_3__0, video_section_3__1, video_section_3__2,
       video_section_3__3, video_section_3__4, video_section_3__5, video_section_3__6, video_section_3__7,
       video_section_4__0, video_section_4__1, video_section_4__2, video_section_4__3, video_section_4__4,
       video_section_4__5, video_section_4__6, video_section_4__7;

  LED led_1 (.in(leds_1_out_33));
  leds leds_1 (
    .player_score(player_score), .cdm8_score(cdm8_score), .out_33(leds_1_out_33), .out_31(leds_1_out_31),
    .out_29(leds_1_out_29), .out_27(leds_1_out_27), .out_25(leds_1_out_25), .out_23(leds_1_out_23),
    .out_21(leds_1_out_21), .out_19(leds_1_out_19), .out_3(leds_1_out_3), .out_5(leds_1_out_5),
    .out_7(leds_1_out_7), .out_9(leds_1_out_9), .out_11(leds_1_out_11), .out_13(leds_1_out_13),
    .out_15(leds_1_out_15), .out_17(leds_1_out_17), .out_4(leds_1_out_4), .out_6(leds_1_out_6),
    .out_8(leds_1_out_8), .out_10(leds_1_out_10), .out_12(leds_1_out_12), .out_14(leds_1_out_14),
    .out_16(leds_1_out_16), .out_18(leds_1_out_18), .out_20(leds_1_out_20), .out_22(leds_1_out_22),
    .out_24(leds_1_out_24), .out_26(leds_1_out_26), .out_28(leds_1_out_28), .out_30(leds_1_out_30),
    .out_32(leds_1_out_32), .out_34(leds_1_out_34));
  LED led_2 (.in(leds_1_out_4));
  LED led_3 (.in(leds_1_out_31));
  LED led_4 (.in(leds_1_out_29));
  LED led_5 (.in(leds_1_out_8));
  LED led_6 (.in(leds_1_out_6));
  dial dial_1 (.\input (player_score), .tens(dial_1_tens), .units(dial_1_units));
  Hex_Digit_Display hex_digit_display_1 (.value(dial_1_tens));  // open: dp
  Button Start (.out(Start_out));
  Joystick #(.bits(2)) joystick_1 (.y(joystick_1_y));  // open: x
  LED led_7 (.in(leds_1_out_25));
  LED led_8 (.in(leds_1_out_27));
  LED led_9 (.in(leds_1_out_10));
  LED led_10 (.in(leds_1_out_12));
  Hex_Digit_Display hex_digit_display_2 (.value(dial_1_units));  // open: dp
  Button Reset (.out(Reset_out));
  DotMatrix #(.matrixcols(32), .matrixrows(32)) dotmatrix_1 (
    .col0(video_section_1__0), .col1(video_section_1__1), .col2(video_section_1__2),
    .col3(video_section_1__3), .col4(video_section_1__4), .col5(video_section_1__5),
    .col6(video_section_1__6), .col7(video_section_1__7), .col8(video_section_2__0),
    .col9(video_section_2__1), .col10(video_section_2__2), .col11(video_section_2__3),
    .col12(video_section_2__4), .col13(video_section_2__5), .col14(video_section_2__6),
    .col15(video_section_2__7), .col16(video_section_3__0), .col17(video_section_3__1),
    .col18(video_section_3__2), .col19(video_section_3__3), .col20(video_section_3__4),
    .col21(video_section_3__5), .col22(video_section_3__6), .col23(video_section_3__7),
    .col24(video_section_4__0), .col25(video_section_4__1), .col26(video_section_4__2),
    .col27(video_section_4__3), .col28(video_section_4__4), .col29(video_section_4__5),
    .col30(video_section_4__6), .col31(video_section_4__7));
  kinematic_controller kinematic_controller_1 (
    .button_up(joystick_1_y), .ID(kinematic_controller_1_id), .ballX(kinematic_controller_1_ballx),
    .ballY(kinematic_controller_1_bally), .leftYout(kinematic_controller_1_leftyout),
    .rightYout(kinematic_controller_1_rightyout), .reset(Reset_out), .out_9(player_score),
    .out_10(cdm8_score), .on_off(Start_out));
  LED led_11 (.in(leds_1_out_23));
  LED led_12 (.in(leds_1_out_21));
  LED led_13 (.in(leds_1_out_14));
  LED led_14 (.in(leds_1_out_16));
  video_section video_section_1 (
    .ID(kinematic_controller_1_id), .x_ball(kinematic_controller_1_ballx),
    .y_ball(kinematic_controller_1_bally), .left_bat(kinematic_controller_1_leftyout),
    .right_bat(kinematic_controller_1_rightyout), .ID_2(video_section_1_id_2),
    .x_ball_2(video_section_1_x_ball_2), .y_ball_2(video_section_1_y_ball_2),
    .left_bat_2(video_section_1_left_bat_2), .right_bat_2(video_section_1_right_bat_2),
    ._0(video_section_1__0), ._1(video_section_1__1), ._2(video_section_1__2), ._3(video_section_1__3),
    ._4(video_section_1__4), ._5(video_section_1__5), ._6(video_section_1__6), ._7(video_section_1__7));
  LED led_15 (.in(leds_1_out_17));
  LED led_16 (.in(leds_1_out_19));
  LED led_17 (.in(leds_1_out_20));
  LED led_18 (.in(leds_1_out_18));
  video_section video_section_2 (
    .ID(video_section_1_id_2), .x_ball(video_section_1_x_ball_2), .y_ball(video_section_1_y_ball_2),
    .left_bat(video_section_1_left_bat_2), .right_bat(video_section_1_right_bat_2),
    .ID_2(video_section_2_id_2), .x_ball_2(video_section_2_x_ball_2), .y_ball_2(video_section_2_y_ball_2),
    .left_bat_2(video_section_2_left_bat_2), .right_bat_2(video_section_2_right_bat_2),
    ._0(video_section_2__0), ._1(video_section_2__1), ._2(video_section_2__2), ._3(video_section_2__3),
    ._4(video_section_2__4), ._5(video_section_2__5), ._6(video_section_2__6), ._7(video_section_2__7));
  LED led_19 (.in(leds_1_out_15));
  LED led_20 (.in(leds_1_out_13));
  LED led_21 (.in(leds_1_out_24));
  LED led_22 (.in(leds_1_out_22));
  video_section video_section_3 (
    .ID(video_section_2_id_2), .x_ball(video_section_2_x_ball_2), .y_ball(video_section_2_y_ball_2),
    .left_bat(video_section_2_left_bat_2), .right_bat(video_section_2_right_bat_2),
    .ID_2(video_section_3_id_2), .x_ball_2(video_section_3_x_ball_2), .y_ball_2(video_section_3_y_ball_2),
    .left_bat_2(video_section_3_left_bat_2), .right_bat_2(video_section_3_right_bat_2),
    ._0(video_section_3__0), ._1(video_section_3__1), ._2(video_section_3__2), ._3(video_section_3__3),
    ._4(video_section_3__4), ._5(video_section_3__5), ._6(video_section_3__6), ._7(video_section_3__7));
  LED led_23 (.in(leds_1_out_11));
  LED led_24 (.in(leds_1_out_9));
  LED led_25 (.in(leds_1_out_26));
  LED led_26 (.in(leds_1_out_28));
  Hex_Digit_Display hex_digit_display_3 (.value(dial_2_tens));  // open: dp
  dial dial_2 (.\input (cdm8_score), .tens(dial_2_tens), .units(dial_2_units));
  video_section video_section_4 (
    .ID(video_section_3_id_2), .x_ball(video_section_3_x_ball_2), .y_ball(video_section_3_y_ball_2),
    .left_bat(video_section_3_left_bat_2), .right_bat(video_section_3_right_bat_2), ._0(video_section_4__0),
    ._1(video_section_4__1), ._2(video_section_4__2), ._3(video_section_4__3), ._4(video_section_4__4),
    ._5(video_section_4__5), ._6(video_section_4__6), ._7(video_section_4__7));  // open: ID_2, x_ball_2, y_ball_2, left_bat_2, right_bat_2
  LED led_27 (.in(leds_1_out_7));
  LED led_28 (.in(leds_1_out_5));
  LED led_29 (.in(leds_1_out_30));
  LED led_30 (.in(leds_1_out_32));
  Hex_Digit_Display hex_digit_display_4 (.value(dial_2_units));  // open: dp
  LED led_31 (.in(leds_1_out_3));
  LED led_32 (.in(leds_1_out_34));
endmodule

module video_chip (
  input  [4:0] ID,
  input  [4:0] x_ball,
  input  [4:0] y_ball,
  input  [4:0] left_bat,
  input  [4:0] right_bat,
  output [4:0] new_ID,
  output [4:0] x_ball_2,
  output [4:0] y_ball_2,
  output [4:0] left_bat_2,
  output [4:0] right_bat_2
);

  inc_5_bit inc_5_bit_1 (.in(ID), .out(new_ID));

  assign left_bat_2 = left_bat;
  assign right_bat_2 = right_bat;
  assign x_ball_2 = x_ball;
  assign y_ball_2 = y_ball;
endmodule

// inc
module inc_5_bit (
  input  [4:0] in,
  output [4:0] out
);

  wire [4:0] and_1_out;

  assign and_1_out = {and_1_out[3:0], 1'b1} & in;  // AND_Gate and_1, 5 bits wide
  assign out = {and_1_out[3:0], 1'b1} ^ in;  // XOR_Gate xor_1, 5 bits wide
  // also tied to GND on the sheet: and_1_out[4]
endmodule

module video_section (
  input  [4:0] ID,
  input  [4:0] x_ball,
  input  [4:0] y_ball,
  input  [4:0] left_bat,
  input  [4:0] right_bat,
  output [31:0] _0,
  output [31:0] _1,
  output [31:0] _2,
  output [31:0] _3,
  output [31:0] _4,
  output [31:0] _5,
  output [31:0] _6,
  output [31:0] _7,
  output [4:0] ID_2,
  output [4:0] x_ball_2,
  output [4:0] y_ball_2,
  output [4:0] left_bat_2,
  output [4:0] right_bat_2
);

  wire comparator_1_eq, comparator_2_eq, comparator_3_eq, comparator_4_eq, comparator_5_eq, comparator_6_eq,
       comparator_7_eq, comparator_8_eq, comparator_9_eq, comparator_10_eq, not_1_out, not_2_out;
  wire [4:0] ID1, ID2, ID3, ID4, ID5, ID6, ID7, video_chip_1_left_bat_2, video_chip_1_right_bat_2,
       video_chip_1_x_ball_2, video_chip_1_y_ball_2, video_chip_2_left_bat_2, video_chip_2_right_bat_2,
       video_chip_2_x_ball_2, video_chip_2_y_ball_2, video_chip_3_left_bat_2, video_chip_3_right_bat_2,
       video_chip_3_x_ball_2, video_chip_3_y_ball_2, video_chip_4_left_bat_2, video_chip_4_right_bat_2,
       video_chip_4_x_ball_2, video_chip_4_y_ball_2, video_chip_5_left_bat_2, video_chip_5_right_bat_2,
       video_chip_5_x_ball_2, video_chip_5_y_ball_2, video_chip_6_left_bat_2, video_chip_6_right_bat_2,
       video_chip_6_x_ball_2, video_chip_6_y_ball_2, video_chip_7_left_bat_2, video_chip_7_right_bat_2,
       video_chip_7_x_ball_2, video_chip_7_y_ball_2;
  wire [31:0] bat_l_32, bat_r_32, multiplexer_2_out, multiplexer_3_out, multiplexer_8_out, multiplexer_9_out,
       y;

  Multiplexer #(.width(32), .enable("false")) multiplexer_1 (
    .in0({32{1'b0}}), .in1(y), .out(_0), .sel(comparator_1_eq));
  _5_to_32 u_5_to_32_1 (.in(y_ball), .out(y));
  Multiplexer #(.width(32), .enable("false")) multiplexer_2 (
    .in0(bat_l_32), .in1({32{1'b0}}), .out(multiplexer_2_out), .sel(not_1_out));
  Comparator #(.width(5)) comparator_1 (.a(ID), .b(x_ball), .eq(comparator_1_eq));  // open: gt, lt
  video_chip video_chip_1 (
    .ID(ID), .x_ball(x_ball), .y_ball(y_ball), .left_bat(left_bat), .right_bat(right_bat), .new_ID(ID1),
    .x_ball_2(video_chip_1_x_ball_2), .y_ball_2(video_chip_1_y_ball_2), .left_bat_2(video_chip_1_left_bat_2),
    .right_bat_2(video_chip_1_right_bat_2));
  assign _1 = multiplexer_2_out | multiplexer_3_out;  // OR_Gate or_1, 32 bits wide
  not not_1 (not_1_out, comparator_3_eq);
  Multiplexer #(.width(32), .enable("false")) multiplexer_3 (
    .in0({32{1'b0}}), .in1(y), .out(multiplexer_3_out), .sel(comparator_2_eq));
  Comparator #(.width(5)) comparator_2 (.a(ID1), .b(x_ball), .eq(comparator_2_eq));  // open: gt, lt
  Comparator #(.width(5)) comparator_3 (.a(ID1), .b(5'b00001), .eq(comparator_3_eq));  // open: gt, lt
  bat bat_1 (.first_y(left_bat_2), .display_col(bat_l_32));
  Multiplexer #(.width(32), .enable("false")) multiplexer_4 (
    .in0({32{1'b0}}), .in1(y), .out(_2), .sel(comparator_4_eq));
  Comparator #(.width(5)) comparator_4 (.a(ID2), .b(x_ball), .eq(comparator_4_eq));  // open: gt, lt
  video_chip video_chip_2 (
    .ID(ID1), .x_ball(video_chip_1_x_ball_2), .y_ball(video_chip_1_y_ball_2),
    .left_bat(video_chip_1_left_bat_2), .right_bat(video_chip_1_right_bat_2), .new_ID(ID2),
    .x_ball_2(video_chip_2_x_ball_2), .y_ball_2(video_chip_2_y_ball_2), .left_bat_2(video_chip_2_left_bat_2),
    .right_bat_2(video_chip_2_right_bat_2));
  Multiplexer #(.width(32), .enable("false")) multiplexer_5 (
    .in0({32{1'b0}}), .in1(y), .out(_3), .sel(comparator_5_eq));
  Comparator #(.width(5)) comparator_5 (.a(ID3), .b(x_ball), .eq(comparator_5_eq));  // open: gt, lt
  video_chip video_chip_3 (
    .ID(ID2), .x_ball(video_chip_2_x_ball_2), .y_ball(video_chip_2_y_ball_2),
    .left_bat(video_chip_2_left_bat_2), .right_bat(video_chip_2_right_bat_2), .new_ID(ID3),
    .x_ball_2(video_chip_3_x_ball_2), .y_ball_2(video_chip_3_y_ball_2), .left_bat_2(video_chip_3_left_bat_2),
    .right_bat_2(video_chip_3_right_bat_2));
  Multiplexer #(.width(32), .enable("false")) multiplexer_6 (
    .in0({32{1'b0}}), .in1(y), .out(_4), .sel(comparator_6_eq));
  video_chip video_chip_4 (
    .ID(ID3), .x_ball(video_chip_3_x_ball_2), .y_ball(video_chip_3_y_ball_2),
    .left_bat(video_chip_3_left_bat_2), .right_bat(video_chip_3_right_bat_2), .new_ID(ID4),
    .x_ball_2(video_chip_4_x_ball_2), .y_ball_2(video_chip_4_y_ball_2), .left_bat_2(video_chip_4_left_bat_2),
    .right_bat_2(video_chip_4_right_bat_2));
  Comparator #(.width(5)) comparator_6 (.a(ID4), .b(x_ball), .eq(comparator_6_eq));  // open: gt, lt
  video_chip video_chip_5 (
    .ID(ID4), .x_ball(video_chip_4_x_ball_2), .y_ball(video_chip_4_y_ball_2),
    .left_bat(video_chip_4_left_bat_2), .right_bat(video_chip_4_right_bat_2), .new_ID(ID5),
    .x_ball_2(video_chip_5_x_ball_2), .y_ball_2(video_chip_5_y_ball_2), .left_bat_2(video_chip_5_left_bat_2),
    .right_bat_2(video_chip_5_right_bat_2));
  Multiplexer #(.width(32), .enable("false")) multiplexer_7 (
    .in0({32{1'b0}}), .in1(y), .out(_5), .sel(comparator_7_eq));
  Comparator #(.width(5)) comparator_7 (.a(ID5), .b(x_ball), .eq(comparator_7_eq));  // open: gt, lt
  video_chip video_chip_6 (
    .ID(ID5), .x_ball(video_chip_5_x_ball_2), .y_ball(video_chip_5_y_ball_2),
    .left_bat(video_chip_5_left_bat_2), .right_bat(video_chip_5_right_bat_2), .new_ID(ID6),
    .x_ball_2(video_chip_6_x_ball_2), .y_ball_2(video_chip_6_y_ball_2), .left_bat_2(video_chip_6_left_bat_2),
    .right_bat_2(video_chip_6_right_bat_2));
  assign _6 = multiplexer_8_out | multiplexer_9_out;  // OR_Gate or_2, 32 bits wide
  Multiplexer #(.width(32), .enable("false")) multiplexer_8 (
    .in0(bat_r_32), .in1({32{1'b0}}), .out(multiplexer_8_out), .sel(not_2_out));
  Multiplexer #(.width(32), .enable("false")) multiplexer_9 (
    .in0({32{1'b0}}), .in1(y), .out(multiplexer_9_out), .sel(comparator_8_eq));
  Comparator #(.width(5)) comparator_8 (.a(ID6), .b(x_ball), .eq(comparator_8_eq));  // open: gt, lt
  Comparator #(.width(5), .mode("unsigned")) comparator_9 (
    .a(ID6), .b(5'b11110), .eq(comparator_9_eq));  // open: gt, lt
  bat bat_2 (.first_y(right_bat_2), .display_col(bat_r_32));
  video_chip video_chip_7 (
    .ID(ID6), .x_ball(video_chip_6_x_ball_2), .y_ball(video_chip_6_y_ball_2),
    .left_bat(video_chip_6_left_bat_2), .right_bat(video_chip_6_right_bat_2), .new_ID(ID7),
    .x_ball_2(video_chip_7_x_ball_2), .y_ball_2(video_chip_7_y_ball_2), .left_bat_2(video_chip_7_left_bat_2),
    .right_bat_2(video_chip_7_right_bat_2));
  Multiplexer #(.width(32), .enable("false")) multiplexer_10 (
    .in0({32{1'b0}}), .in1(y), .out(_7), .sel(comparator_10_eq));
  not not_2 (not_2_out, comparator_9_eq);
  Comparator #(.width(5)) comparator_10 (.a(ID7), .b(x_ball), .eq(comparator_10_eq));  // open: gt, lt
  video_chip video_chip_8 (
    .ID(ID7), .x_ball(video_chip_7_x_ball_2), .y_ball(video_chip_7_y_ball_2),
    .left_bat(video_chip_7_left_bat_2), .right_bat(video_chip_7_right_bat_2), .new_ID(ID_2),
    .x_ball_2(x_ball_2), .y_ball_2(y_ball_2), .left_bat_2(left_bat_2), .right_bat_2(right_bat_2));

  // Other names for the same wires on the sheet: bat_l[4:0] = left_bat_2; bat_r[4:0] = right_bat_2; ID0[4:0] = ID;
  //   x[4:0] = x_ball
endmodule

// CONTROLLER
module kinematic_controller (
  input  reset,
  input  on_off,
  input  [1:0] button_up,
  output [4:0] ID,
  output [4:0] ballX,
  output [4:0] ballY,
  output [4:0] leftYout,
  output [4:0] rightYout,
  output [7:0] out_9,
  output [7:0] out_10
);

  wire clock_1_out, clock_2_out, clock_3_out, clock_4_out, controlled_buffer_1_out, controlled_buffer_2_out,
       controlled_buffer_3_out, controlled_buffer_4_out, controlled_buffer_5_out, counter_1_q,
       counter_2_carry, down, game_over, hitTheLeftBall, hitTheRightBall, init, on_off_t, or_1_out, undriven,
       up, x, y;
  wire [2:0] left_bat_out, right_bat_out, x_ball, y_ball;
  wire [7:0] cdm8_bat, left_bat, multiplexer_1_out, multiplexer_2_out, multiplexer_3_out, multiplexer_4_out,
       right_bat, vx, vx_out, vy, vy_out, x_ball_out, y_ball_out;

  bat_move bat_move_1 (.bat_y({leftYout, left_bat_out}), .new_bat_y(left_bat), .up(up), .down(down));
  check_hit check_hit_1 (
    .ball_x(x_ball_out), .x_hit(x), .left_bat(left_bat), .vx(vx_out), .vy(vy_out), .ball_y(y_ball_out),
    .y_hit(y), .hit_the_right_wall(hitTheRightBall), .hit_the_left_wall(hitTheLeftBall), .right_bat(right_bat));
  cdm8 cdm8_1 (
    .p_score(out_9), .cdm8_score(out_10), .ball_x(x_ball_out), .ball_y(y_ball_out), .vx(vx_out), .vy(vy_out),
    .cdm8_bat(cdm8_bat), .reset(reset), .on_off(on_off_t));
  Comparator #(.width(2), .mode("unsigned")) comparator_1 (.a(2'b10), .b(button_up), .gt(up), .lt(down));  // open: eq
  cdm8_bat_move cdm8_bat_move_1 (.new_y(right_bat), .current_y({rightYout, right_bat_out}), .calculated_y(cdm8_bat));
  Clock #(.highDuration(2), .lowDuration(2)) clock_1 (.out(clock_1_out));
  Clock #(.highDuration(4), .lowDuration(4)) clock_2 (.out(clock_2_out));
  Multiplexer #(.width(8), .enable("false")) multiplexer_1 (
    .in0({ballX, x_ball}), .in1(8'h78), .out(multiplexer_1_out), .sel(init));
  Register u_x (.D(multiplexer_1_out), .Q(x_ball_out), .clk(controlled_buffer_1_out));  // open: en, clr
  Register u_vx (.D(multiplexer_2_out), .Q(vx_out), .clk(controlled_buffer_1_out));  // open: en, clr
  Multiplexer #(.width(8), .enable("false")) multiplexer_2 (
    .in0(vx), .in1({8{1'b1}}), .out(multiplexer_2_out), .sel(init));
  assign controlled_buffer_1_out = game_over ? clock_1_out : 1'bz;  // Controlled_Buffer controlled_buffer_1
  Counter player_score (
    .count(hitTheRightBall), .Q(out_9), .clk(controlled_buffer_1_out), .clr(reset));  // open: load, D, carry
  Register leftYreg (
    .D(left_bat), .Q({leftYout, left_bat_out}), .clk(controlled_buffer_3_out), .clr(reset));  // open: en
  assign controlled_buffer_2_out = game_over ? clock_2_out : 1'bz;  // Controlled_Buffer controlled_buffer_2
  assign controlled_buffer_3_out = or_1_out ? controlled_buffer_2_out : 1'bz;  // Controlled_Buffer controlled_buffer_3
  or or_1 (or_1_out, up, down);
  Multiplexer #(.width(8), .enable("false")) multiplexer_3 (
    .in0({ballY, y_ball}), .in1(8'h78), .out(multiplexer_3_out), .sel(init));
  Multiplexer #(.width(8), .enable("false")) multiplexer_4 (.in0(vy), .in1(8'h2), .out(multiplexer_4_out), .sel(init));
  assign controlled_buffer_4_out = game_over ? clock_3_out : 1'bz;  // Controlled_Buffer controlled_buffer_4
  Clock clock_3 (.out(clock_3_out));
  game_over game_over_1 (.player_score(out_10), .cdm8_score(out_9), .game_over(game_over));
  Register u_y (.D(multiplexer_3_out), .Q(y_ball_out), .clk(controlled_buffer_1_out));  // open: en, clr
  Register u_vy (.D(multiplexer_4_out), .Q(vy_out), .clk(controlled_buffer_1_out));  // open: en, clr
  Counter cdm8_score (
    .count(hitTheLeftBall), .Q(out_10), .clk(controlled_buffer_1_out), .clr(reset));  // open: load, D, carry
  Register rightYreg (
    .D(right_bat), .Q({rightYout, right_bat_out}), .clk(controlled_buffer_4_out), .clr(reset));  // open: en
  Clock #(.highDuration(4), .lowDuration(4)) clock_4 (.out(clock_4_out));
  assign controlled_buffer_5_out = on_off_t ? clock_4_out : 1'bz;  // Controlled_Buffer controlled_buffer_5
  ball_move ball_move_1 (
    .crash_x(x), .crash_y(y), .vx(vx_out), .vy(vy_out), .ball_x(x_ball_out), .ball_y(y_ball_out),
    .new_ball_x({ballX, x_ball}), .new_ball_y({ballY, y_ball}), .new_vx(vx), .new_vy(vy));
  Counter #(.width(1), .max('h1)) counter_1 (
    .count(init), .Q(counter_1_q), .clk(controlled_buffer_5_out), .clr(reset));  // open: load, D, carry
  Counter #(.width(1), .max('h1)) counter_2 (
    .Q(on_off_t), .carry(counter_2_carry), .clk(on_off), .clr(undriven));  // open: load, D, count
  Comparator #(.width(1), .mode("unsigned")) comparator_2 (.a(1'b0), .b(counter_1_q), .eq(init));  // open: gt, lt

  assign ID = {5{1'b0}};

  // Other names for the same wires on the sheet: y_ball[7:3] = ballY; cdm8_score[7:0] = out_10;
  //   left_bat_out[7:3] = leftYout; player_score[7:0] = out_9; right_bat_out[7:3] = rightYout; x_ball[7:3] = ballX
endmodule

module inc_3_bit (
  input  [2:0] in,
  output [2:0] out
);

  wire [2:0] and_1_out;

  assign and_1_out = {and_1_out[1:0], 1'b1} & in;  // AND_Gate and_1, 3 bits wide
  assign out = {and_1_out[1:0], 1'b1} ^ in;  // XOR_Gate xor_1, 3 bits wide
  // also tied to GND on the sheet: and_1_out[2]
endmodule

// conv
module _5_to_32 (
  input  [4:0] in,
  output [31:0] out
);

  Shifter #(.width(32)) shifter_1 (.in(32'h1), .\dist (in), .out(out));
endmodule

module bat (
  input  [4:0] first_y,
  output [31:0] display_col
);

  wire [31:0] adder_1_out, adder_2_out, n5_to_32_1_out, shifter_1_out, shifter_2_out, shifter_3_out;

  _5_to_32 u_5_to_32_1 (.in(first_y), .out(n5_to_32_1_out));
  Shifter #(.width(32)) shifter_1 (.in(n5_to_32_1_out), .\dist (5'b00001), .out(shifter_1_out));
  Shifter #(.width(32)) shifter_2 (.in(shifter_1_out), .\dist (5'b00001), .out(shifter_2_out));
  Adder #(.width(32)) adder_1 (.a(shifter_1_out), .b(n5_to_32_1_out), .out(adder_1_out));  // open: cin, cout
  Shifter #(.width(32)) shifter_3 (.in(shifter_2_out), .\dist (5'b00001), .out(shifter_3_out));
  Adder #(.width(32)) adder_2 (.a(shifter_2_out), .b(adder_1_out), .out(adder_2_out));  // open: cin, cout
  Adder #(.width(32)) adder_3 (.a(shifter_3_out), .b(adder_2_out), .out(display_col));  // open: cin, cout
endmodule

// left_bat
module bat_move (
  input  [7:0] bat_y,
  input  up,
  input  down,
  output [7:0] new_bat_y
);

  wire adder_1_cout, adder_2_cout, adder_3_cout, controlled_buffer_1_out, not_1_out, or_1_out,
       pull_resistor_2_node;
  wire [7:0] adder_2_out, adder_3_out, multiplexer_1_out, multiplexer_2_out;

  Adder adder_1 (.a(bat_y), .b(8'h21), .cout(adder_1_cout));  // open: out, cin
  or or_1 (or_1_out, adder_1_cout, adder_2_cout);
  not not_1 (not_1_out, or_1_out);
  assign controlled_buffer_1_out = not_1_out ? up : 1'bz;  // Controlled_Buffer controlled_buffer_1
  Adder adder_2 (.a(bat_y), .b(8'h7), .out(adder_2_out), .cout(adder_2_cout));  // open: cin
  Pull_Resistor pull_resistor_1 (.node(controlled_buffer_1_out));
  Adder adder_3 (.a(bat_y), .b(8'hf9), .out(adder_3_out), .cout(adder_3_cout));  // open: cin
  Pull_Resistor pull_resistor_2 (.node(pull_resistor_2_node));
  assign pull_resistor_2_node = adder_3_cout ? down : 1'bz;  // Controlled_Buffer controlled_buffer_2
  Multiplexer #(.width(8), .enable("false")) multiplexer_1 (
    .in0(bat_y), .in1(adder_2_out), .out(multiplexer_1_out), .sel(controlled_buffer_1_out));
  Multiplexer #(.width(8), .enable("false")) multiplexer_2 (
    .in0(bat_y), .in1(adder_3_out), .out(multiplexer_2_out), .sel(pull_resistor_2_node));
  Multiplexer #(.width(8), .enable("false")) multiplexer_3 (
    .in0(multiplexer_1_out), .in1(multiplexer_2_out), .out(new_bat_y), .sel(pull_resistor_2_node));
endmodule

module leds (
  input  [7:0] player_score,
  input  [7:0] cdm8_score,
  output out_3,
  output out_4,
  output out_5,
  output out_6,
  output out_7,
  output out_8,
  output out_9,
  output out_10,
  output out_11,
  output out_12,
  output out_13,
  output out_14,
  output out_15,
  output out_16,
  output out_17,
  output out_18,
  output out_19,
  output out_20,
  output out_21,
  output out_22,
  output out_23,
  output out_24,
  output out_25,
  output out_26,
  output out_27,
  output out_28,
  output out_29,
  output out_30,
  output out_31,
  output out_32,
  output out_33,
  output out_34
);

  wire clock_1_out, comparator_1_eq, comparator_1_gt, comparator_2_eq, comparator_2_gt,
       controlled_buffer_1_out, controlled_buffer_2_out, or_1_out, or_2_out, or_3_out;
  wire [31:0] multiplexer_1_out, multiplexer_3_out;

  Comparator comparator_1 (.a(player_score), .b(8'h18), .gt(comparator_1_gt), .eq(comparator_1_eq));  // open: lt
  Comparator comparator_2 (.a(cdm8_score), .b(8'h18), .gt(comparator_2_gt), .eq(comparator_2_eq));  // open: lt
  or or_1 (or_1_out, comparator_1_gt, comparator_1_eq);
  or or_2 (or_2_out, comparator_2_gt, comparator_2_eq);
  or or_3 (or_3_out, or_1_out, or_2_out);
  Multiplexer #(.width(32), .enable("false")) multiplexer_1 (
    .in0(32'h55555555), .in1(32'haaaaaaaa), .out(multiplexer_1_out), .sel(controlled_buffer_1_out));
  assign controlled_buffer_1_out = or_3_out ? clock_1_out : 1'bz;  // Controlled_Buffer controlled_buffer_1
  Multiplexer #(.width(32), .enable("false")) multiplexer_2 (
    .in0(multiplexer_1_out), .in1(multiplexer_3_out),
    .out({out_33, out_31, out_29, out_27, out_25, out_23, out_21, out_19, out_17, out_15, out_13, out_11, out_9, out_7, out_5, out_3, out_4, out_6, out_8, out_10, out_12, out_14, out_16, out_18, out_20, out_22, out_24, out_26, out_28, out_30, out_32, out_34}),
    .sel(or_2_out));
  Multiplexer #(.width(32), .enable("false")) multiplexer_3 (
    .in0({32{1'b1}}), .in1({32{1'b0}}), .out(multiplexer_3_out), .sel(controlled_buffer_2_out));
  assign controlled_buffer_2_out = or_3_out ? clock_1_out : 1'bz;  // Controlled_Buffer controlled_buffer_2
  Clock #(.highDuration(100), .lowDuration(100)) clock_1 (.out(clock_1_out));
endmodule

module ball_move (
  input  crash_x,
  input  crash_y,
  input  [7:0] vx,
  input  [7:0] vy,
  input  [7:0] ball_x,
  input  [7:0] ball_y,
  output [7:0] new_ball_x,
  output [7:0] new_ball_y,
  output [7:0] new_vx,
  output [7:0] new_vy
);

  wire [7:0] multiplexer_1_out, multiplexer_2_out, neg_vx, neg_vy, not_1_out, not_2_out;

  assign not_1_out = ~vx;  // NOT_Gate not_1, 8 bits wide
  inc_8_bit inc_8_bit_1 (.in(not_1_out), .out(neg_vx));
  assign not_2_out = ~vy;  // NOT_Gate not_2, 8 bits wide
  inc_8_bit inc_8_bit_2 (.in(not_2_out), .out(neg_vy));
  Multiplexer #(.width(8), .enable("false")) multiplexer_1 (
    .in0(vx), .in1(neg_vx), .out(multiplexer_1_out), .sel(crash_x));
  Multiplexer #(.width(8), .enable("false")) multiplexer_2 (
    .in0(vy), .in1(neg_vy), .out(multiplexer_2_out), .sel(crash_y));
  Adder adder_1 (.a(multiplexer_1_out), .b(ball_x), .out(new_ball_x));  // open: cin, cout
  Adder adder_2 (.a(multiplexer_2_out), .b(ball_y), .out(new_ball_y));  // open: cin, cout
  Multiplexer #(.width(8), .enable("false")) multiplexer_3 (.in0(vx), .in1(neg_vx), .out(new_vx), .sel(crash_x));
  Multiplexer #(.width(8), .enable("false")) multiplexer_4 (.in0(vy), .in1(neg_vy), .out(new_vy), .sel(crash_y));

  // Other names for the same wires on the sheet: bx[7:0] = ball_x; by[7:0] = ball_y
endmodule

module check_hit (
  input  [7:0] left_bat,
  input  [7:0] ball_x,
  input  [7:0] vy,
  input  [7:0] ball_y,
  input  [7:0] right_bat,
  input  [7:0] vx,
  output y_hit,
  output x_hit,
  output hit_the_right_wall,
  output hit_the_left_wall
);

  wire adder_1_cout, adder_2_cout, adder_5_cout, adder_6_cout, and_2_out, and_3_out, and_4_out, and_5_out,
       and_6_out, check_carry_2_r, comparator_1_lt, comparator_2_gt, comparator_3_lt, comparator_4_eq,
       comparator_4_gt, comparator_5_eq, comparator_6_lt, comparator_7_eq, comparator_7_gt, comparator_8_eq,
       comparator_9_lt, comparator_10_gt, or_1_out, or_2_out, or_3_out;
  wire [15:0] adder_3_out, adder_4_out, bit_extender_1_out, bit_extender_2_out, bit_extender_3_out,
       bit_extender_4_out;

  Adder adder_1 (.a(ball_x), .b(vx), .cout(adder_1_cout));  // open: out, cin
  Comparator comparator_1 (.a(vx), .b({8{1'b0}}), .lt(comparator_1_lt));  // open: gt, eq
  assign bit_extender_1_out = {{8{1'b0}}, {left_bat[7:3], 3'b000}};  // Bit_Extender bit_extender_1
  assign bit_extender_2_out = {{8{1'b0}}, {right_bat[7:3], 3'b000}};  // Bit_Extender bit_extender_2
  Adder adder_2 (.a(vx), .b(ball_x), .cout(adder_2_cout));  // open: out, cin
  and and_1 (hit_the_right_wall, adder_2_cout, comparator_2_gt);
  check_carry check_carry_1 (.a(comparator_1_lt), .b(adder_1_cout), .r(hit_the_left_wall));
  Adder #(.width(16)) adder_3 (.a(16'h21), .b(bit_extender_1_out), .out(adder_3_out));  // open: cin, cout
  assign bit_extender_3_out = {{8{1'b0}}, ball_y};  // Bit_Extender bit_extender_3
  Adder #(.width(16)) adder_4 (.a(16'h21), .b(bit_extender_2_out), .out(adder_4_out));  // open: cin, cout
  Comparator comparator_2 (.a(vx), .b({8{1'b0}}), .gt(comparator_2_gt));  // open: eq, lt
  or or_1 (or_1_out, hit_the_right_wall, hit_the_left_wall);
  Comparator #(.width(16), .mode("unsigned")) comparator_3 (
    .a(bit_extender_3_out), .b(adder_3_out), .lt(comparator_3_lt));  // open: gt, eq
  Comparator #(.mode("unsigned")) comparator_4 (
    .a(ball_y), .b({left_bat[7:3], 3'b000}), .gt(comparator_4_gt), .eq(comparator_4_eq));  // open: lt
  Comparator #(.width(5), .mode("unsigned")) comparator_5 (
    .a(5'b00001), .b(ball_x[7:3]), .eq(comparator_5_eq));  // open: gt, lt
  assign bit_extender_4_out = {{8{1'b0}}, ball_y};  // Bit_Extender bit_extender_4
  or or_2 (or_2_out, comparator_4_gt, comparator_4_eq);
  Comparator #(.width(16), .mode("unsigned")) comparator_6 (
    .a(bit_extender_4_out), .b(adder_4_out), .lt(comparator_6_lt));  // open: gt, eq
  Comparator #(.mode("unsigned")) comparator_7 (
    .a(ball_y), .b({right_bat[7:3], 3'b000}), .gt(comparator_7_gt), .eq(comparator_7_eq));  // open: lt
  or or_3 (or_3_out, comparator_7_gt, comparator_7_eq);
  Comparator #(.width(5), .mode("unsigned")) comparator_8 (
    .a(5'b11110), .b(ball_x[7:3]), .eq(comparator_8_eq));  // open: gt, lt
  and and_2 (and_2_out, comparator_3_lt, or_2_out);
  and and_3 (and_3_out, comparator_6_lt, or_3_out);
  and and_4 (and_4_out, and_2_out, comparator_5_eq);
  and and_5 (and_5_out, and_3_out, comparator_8_eq);
  Adder adder_5 (.a(vy), .b(ball_y), .cout(adder_5_cout));  // open: out, cin
  and and_6 (and_6_out, adder_5_cout, comparator_10_gt);
  Adder adder_6 (.a(ball_y), .b(vy), .cout(adder_6_cout));  // open: out, cin
  check_carry check_carry_2 (.a(comparator_9_lt), .b(adder_6_cout), .r(check_carry_2_r));
  Comparator comparator_9 (.a(vy), .b({8{1'b0}}), .lt(comparator_9_lt));  // open: gt, eq
  Comparator comparator_10 (.a(vy), .b({8{1'b0}}), .gt(comparator_10_gt));  // open: eq, lt
  or or_4 (y_hit, and_6_out, check_carry_2_r);
  or or_5 (x_hit, and_4_out, and_5_out, or_1_out);

  // Other names for the same wires on the sheet: x[7:0] = ball_x; y[7:0] = ball_y
endmodule

module inc_8_bit (
  input  [7:0] in,
  output [7:0] out
);

  wire [7:0] and_1_out;

  assign and_1_out = {and_1_out[6:0], 1'b1} & in;  // AND_Gate and_1, 8 bits wide
  assign out = {and_1_out[6:0], 1'b1} ^ in;  // XOR_Gate xor_1, 8 bits wide
  // also tied to GND on the sheet: and_1_out[7]
endmodule

module check_carry (
  input  a,
  input  b,
  output r
);

  wire transistor_1_out;

  Transistor #(.\type ("n")) transistor_1 (.in(1'b1), .out(transistor_1_out), .gate(a));
  Transistor #(.gate("br")) transistor_2 (.in(transistor_1_out), .out(r), .gate(b));
  Pull_Resistor pull_resistor_1 (.node(r));
endmodule

// right_bat
module cdm8_bat_move (
  input  [7:0] current_y,
  input  [7:0] calculated_y,
  output [7:0] new_y
);

  wire adder_1_cout, adder_2_cout, adder_3_cout, comparator_1_gt, comparator_1_lt, controlled_buffer_1_out,
       controlled_buffer_2_out, not_1_out, or_1_out;
  wire [7:0] adder_2_out, adder_3_out, multiplexer_1_out, multiplexer_2_out;

  Comparator #(.mode("unsigned")) comparator_1 (
    .a(current_y), .b(calculated_y), .gt(comparator_1_gt), .lt(comparator_1_lt));  // open: eq
  Adder adder_1 (.a(current_y), .b(8'h21), .cout(adder_1_cout));  // open: out, cin
  or or_1 (or_1_out, adder_1_cout, adder_2_cout);
  not not_1 (not_1_out, or_1_out);
  assign controlled_buffer_1_out = not_1_out ? comparator_1_lt : 1'bz;  // Controlled_Buffer controlled_buffer_1
  Adder adder_2 (.a(current_y), .b(8'h1), .out(adder_2_out), .cout(adder_2_cout));  // open: cin
  Adder adder_3 (.a(current_y), .b({8{1'b1}}), .out(adder_3_out), .cout(adder_3_cout));  // open: cin
  assign controlled_buffer_2_out = adder_3_cout ? comparator_1_gt : 1'bz;  // Controlled_Buffer controlled_buffer_2
  Multiplexer #(.width(8), .enable("false")) multiplexer_1 (
    .in0(current_y), .in1(adder_2_out), .out(multiplexer_1_out), .sel(controlled_buffer_1_out));
  Pull_Resistor pull_resistor_1 (.node(controlled_buffer_1_out));
  Multiplexer #(.width(8), .enable("false")) multiplexer_2 (
    .in0(current_y), .in1(adder_3_out), .out(multiplexer_2_out), .sel(controlled_buffer_2_out));
  Pull_Resistor pull_resistor_2 (.node(controlled_buffer_2_out));
  Multiplexer #(.width(8), .enable("false")) multiplexer_3 (
    .in0(multiplexer_1_out), .in1(multiplexer_2_out), .out(new_y), .sel(controlled_buffer_2_out));
endmodule

// cdm8 with banks
module cdm8 (
  input  reset,
  input  on_off,
  input  [7:0] p_score,
  input  [7:0] cdm8_score,
  input  [7:0] ball_x,
  input  [7:0] ball_y,
  input  [7:0] vx,
  input  [7:0] vy,
  output [7:0] cdm8_bat
);

  wire and_2_out, and_3_out, cdm_8_mark5_1_p4, cdm_8_mark5_1_p5, cdm_8_mark5_1_p7, cdm_8_mark5_1_p8,
       cdm_8_mark5_1_p10, cdm_8_mark5_1_p11, clk, clk1, clock_1_out, comparator_1_eq, comparator_2_eq,
       controlled_buffer_4_out, d_ff_1_q, decoder_1_out0, decoder_1_out1, IAck, IOsel, IRQ,
       multiplexer_1_out, multiplexer_4_out, not_1_out, not_2_out, not_3_out, not_4_out, of, or_1_out, ram,
       READwrite, register_2_q;
  wire [2:0] cnt, vec;
  wire [7:0] addr, address, bit_extender_1_out, cdm_8_mark5_1_p14, cdm_8_mark5_1_p15, IOdat,
       multiplexer_2_out, multiplexer_3_out, pc;

  // Probe on cdm_8_mark5_1_p8
  // Probe on cdm_8_mark5_1_p7
  // Probe on cdm_8_mark5_1_p5
  // Probe on cdm_8_mark5_1_p4
  Multiplexer multiplexer_1 (.in0(1'b0), .in1(clk), .out(multiplexer_1_out), .sel(ram), .en(of));
  // Probe on pc
  // CdM_8_mark5 cdm_8_mark5_1: pin names not known; wires that end beside it: IRQ, vec, IAck, cdm_8_mark5_1_p4, cdm_8_mark5_1_p5, multiplexer_1_out, cdm_8_mark5_1_p7, cdm_8_mark5_1_p8, pc, cdm_8_mark5_1_p10, cdm_8_mark5_1_p11, READwrite, address, cdm_8_mark5_1_p14, cdm_8_mark5_1_p15
  Multiplexer #(.select(3), .width(8), .enable("false")) multiplexer_2 (
    .in0(p_score), .in1(cdm8_score), .in2(cdm8_bat), .in3(ball_x), .in4(ball_y), .in5(vx), .in6(vy),
    .in7(IOdat), .out(multiplexer_2_out), .sel(cnt));
  and and_1 (IOsel, address[4], address[5], address[6], address[7], decoder_1_out1);
  Decoder #(.disabled(0)) decoder_1 (
    .out0(decoder_1_out0), .out1(decoder_1_out1), .sel(cdm_8_mark5_1_p10), .en(cdm_8_mark5_1_p11));
  not not_1 (not_1_out, READwrite);
  assign IOdat = not_1_out ? cdm_8_mark5_1_p14 : 8'bz;  // Controlled_Buffer controlled_buffer_1
  assign cdm_8_mark5_1_p15 = READwrite ? IOdat : 8'bz;  // Controlled_Buffer controlled_buffer_2
  Multiplexer #(.width(8), .enable("false")) multiplexer_3 (
    .in0(addr), .in1(address), .out(multiplexer_3_out), .sel(and_2_out));
  and and_2 (and_2_out, ram, of);
  and and_3 (and_3_out, decoder_1_out1, ~IOsel);  // AND_Gate
  Comparator comparator_1 (.a(8'he2), .b(address), .eq(comparator_1_eq));  // open: gt, lt
  or or_1 (or_1_out, and_3_out, ~of);  // OR_Gate
  not not_2 (not_2_out, clk);
  Register register_1 (.D(IOdat), .Q(cdm8_bat), .clk(comparator_1_eq));  // open: en, clr
  RAM #(.bus("separate")) ram_1 (
    .addr(multiplexer_3_out), .din(multiplexer_2_out), .data(IOdat), .sel(or_1_out), .clk(not_2_out),
    .ld(multiplexer_4_out), .clr(reset));  // open: str
  Multiplexer #(.enable("false")) multiplexer_4 (.in0(1'b0), .in1(READwrite), .out(multiplexer_4_out), .sel(of));
  ROM rom_1 (.addr(address), .data(IOdat), .sel(decoder_1_out0));
  Clock clock_1 (.out(clock_1_out));
  assign clk = on_off ? clock_1_out : 1'bz;  // Controlled_Buffer controlled_buffer_3
  Multiplexer #(.enable("false")) multiplexer_5 (.in0(clk), .in1(1'b0), .out(clk1), .sel(d_ff_1_q));
  Pull_Resistor pull_resistor_1 (.node(clk));
  D_Flip_Flop d_ff_1 (.clk(of), .D(of), .Q(d_ff_1_q), .reset(comparator_2_eq));  // open: Qn, preset, en
  D_Flip_Flop #(.trigger("high")) d_ff_2 (.clk(d_ff_1_q), .D(d_ff_1_q), .Q(ram));  // open: Qn, preset, en, reset
  assign bit_extender_1_out = {{5{1'b0}}, cnt};  // Bit_Extender bit_extender_1
  Counter #(.width(3), .max('h7)) counter_1 (
    .Q(cnt), .carry(of), .clk(clk1), .clr(controlled_buffer_4_out));  // open: load, D, count
  assign controlled_buffer_4_out = of ? register_2_q : 1'bz;  // Controlled_Buffer controlled_buffer_4
  not not_3 (not_3_out, register_2_q);
  Comparator comparator_2 (.a(pc), .b(8'h2b), .eq(comparator_2_eq));  // open: gt, lt
  Adder adder_1 (.a(8'he0), .b(bit_extender_1_out), .out(addr));  // open: cin, cout
  Register #(.width(1)) register_2 (
    .D(not_3_out), .Q(register_2_q), .clk(comparator_2_eq), .clr(not_4_out));  // open: en
  not not_4 (not_4_out, of);

  // Other names for the same wires on the sheet: IOaddr[3:0] = address[3:0]; bat[7:0] = cdm8_bat;
  //   player_score[7:0] = p_score

  // Notes on the sheet:
  //   contents of rom_1 (hex, n*v repeats v):
  //   cd f0 d1 e3 b5 d3 e5 bf f e4 e 5 e5 10 ee 2b d0 f0 31 5 99 d3 e6 bf f e5 1c 85 d2 e4 ba 19 e3 25 d2
  //   ff 36 d3 ff 3e d0 e2 a2 ee 2 d7 d4
endmodule

module game_over (
  input  [7:0] player_score,
  input  [7:0] cdm8_score,
  output game_over
);

  wire comparator_1_eq, comparator_1_gt, comparator_2_eq, comparator_2_gt, or_1_out, or_2_out, or_3_out;

  Comparator comparator_1 (.a(player_score), .b(8'h18), .gt(comparator_1_gt), .eq(comparator_1_eq));  // open: lt
  Comparator comparator_2 (.a(cdm8_score), .b(8'h18), .gt(comparator_2_gt), .eq(comparator_2_eq));  // open: lt
  or or_1 (or_1_out, comparator_1_gt, comparator_1_eq);
  or or_2 (or_2_out, comparator_2_gt, comparator_2_eq);
  or or_3 (or_3_out, or_1_out, or_2_out);
  not not_1 (game_over, or_3_out);

  // Notes on the sheet:
  //   game_over: pull=up
endmodule

module dial (
  input  [7:0] \input ,
  output [3:0] tens,
  output [3:0] units
);

  wire [3:0] tens_units_1_out_tens, tens_units_2_out_tens, tens_units_3_out_tens, tens_units_4_out_tens,
       tens_units_5_out_tens;
  wire [7:0] tens_units_1_out_units, tens_units_2_out_units, tens_units_3_out_units, tens_units_4_out_units,
       tens_units_5_out_units;
  wire [7:4] tens_units_6_out_units;

  tens_units tens_units_1 (
    .in_units(\input ), .in_tens(4'b0000), .out_units(tens_units_1_out_units),
    .out_tens(tens_units_1_out_tens));
  tens_units tens_units_2 (
    .in_units(tens_units_3_out_units), .in_tens(tens_units_3_out_tens), .out_units(tens_units_2_out_units),
    .out_tens(tens_units_2_out_tens));
  tens_units tens_units_3 (
    .in_units(tens_units_1_out_units), .in_tens(tens_units_1_out_tens), .out_units(tens_units_3_out_units),
    .out_tens(tens_units_3_out_tens));
  tens_units tens_units_4 (
    .in_units(tens_units_2_out_units), .in_tens(tens_units_2_out_tens), .out_units(tens_units_4_out_units),
    .out_tens(tens_units_4_out_tens));
  tens_units tens_units_5 (
    .in_units(tens_units_4_out_units), .in_tens(tens_units_4_out_tens), .out_units(tens_units_5_out_units),
    .out_tens(tens_units_5_out_tens));
  tens_units tens_units_6 (
    .in_units(tens_units_5_out_units), .in_tens(tens_units_5_out_tens),
    .out_units({tens_units_6_out_units, units}), .out_tens(tens));
endmodule

module tens_units (
  input  [7:0] in_units,
  input  [3:0] in_tens,
  output [7:0] out_units,
  output [3:0] out_tens
);

  wire comparator_1_lt;
  wire [0:0] not_1_out;
  wire [7:0] subtractor_1_out;

  Comparator #(.mode("unsigned")) comparator_1 (.a(in_units), .b(8'ha), .lt(comparator_1_lt));  // open: gt, eq
  Subtractor subtractor_1 (.a(in_units), .b(8'ha), .out(subtractor_1_out));  // open: bin, bout
  not not_1 (not_1_out[0], comparator_1_lt);
  Multiplexer #(.width(8), .enable("false")) multiplexer_1 (
    .in0(subtractor_1_out), .in1(in_units), .out(out_units), .sel(comparator_1_lt));
  Adder #(.width(4)) adder_1 (.a({3'b000, not_1_out[0]}), .b(in_tens), .out(out_tens));  // open: cin, cout
endmodule
